// Logisim project 2_to_4_DEC.circ as structural Verilog: 8 circuits, main circuit main
module main (
  input  in_1,
  input  in_2,
  input  in_3,
  input  in_4,
  input  in_5,
  input  in_6,
  input  in_7,
  input  in_8,
  input  in_9,
  input  in_10
);

  wire and_1_out, dec_2to4_1_y0, dec_2to4_1_y1, dec_2to4_1_y2, dec_2to4_1_y3, dec_3to8_1_y0, dec_3to8_1_y1,
       dec_3to8_1_y2, dec_3to8_1_y3, dec_3to8_1_y4, dec_3to8_1_y5, dec_3to8_1_y6, dec_3to8_1_y7, nand_1_out,
       nand_2_out, nand_3_out, or_1_out, or_2_out;

  nand nand_1 (nand_1_out, in_1, in_2);
  or or_1 (or_1_out, in_1, in_2);
  nand nand_2 (nand_2_out, in_3, in_4);
  or or_2 (or_2_out, in_3, in_4);
  and and_1 (and_1_out, nand_1_out, or_1_out);
  LED XOR_OUT (.in(and_1_out));
  nand nand_3 (nand_3_out, nand_2_out, or_2_out);
  LED XNOR_OUT (.in(nand_3_out));
  DEC_2To4 dec_2to4_1 (
    .A0(in_5), .A1(in_6), .Y0(dec_2to4_1_y0), .Y1(dec_2to4_1_y1), .Y2(dec_2to4_1_y2), .Y3(dec_2to4_1_y3));
  DEC_3To8 dec_3to8_1 (
    .A0(in_7), .A1(in_8), .A2(in_9), .Y0(dec_3to8_1_y0), .Y1(dec_3to8_1_y1), .Y2(dec_3to8_1_y2),
    .Y3(dec_3to8_1_y3), .Y4(dec_3to8_1_y4), .Y5(dec_3to8_1_y5), .Y6(dec_3to8_1_y6), .Y7(dec_3to8_1_y7));
  LED led_1 (.in(dec_2to4_1_y0));
  LED led_2 (.in(dec_2to4_1_y1));
  LED led_3 (.in(dec_2to4_1_y2));
  LED led_4 (.in(dec_2to4_1_y3));
  LedBar ledbar_1 (
    .led0(dec_3to8_1_y0), .led1(dec_3to8_1_y1), .led2(dec_3to8_1_y2), .led3(dec_3to8_1_y3),
    .led4(dec_3to8_1_y4), .led5(dec_3to8_1_y5), .led6(dec_3to8_1_y6), .led7(dec_3to8_1_y7));
  Hex_Digit_Display hex_digit_display_1 ();  // open: value, dp
endmodule

module DEC_2To4 (
  input  A0,
  input  A1,
  output Y0,
  output Y1,
  output Y2,
  output Y3
);

  wire not_1_out, not_2_out;

  not not_1 (not_1_out, A0);
  not not_2 (not_2_out, A1);
  and and_1 (Y0, not_1_out, not_2_out);
  and and_2 (Y1, not_2_out, A0);
  and and_3 (Y2, not_1_out, A1);
  and and_4 (Y3, A0, A1);
endmodule

module Half_Adder (
  input  A0,
  input  A1,
  output SUM,
  output CAL
);

  xor xor_1 (SUM, A0, A1);
  and and_1 (CAL, A0, A1);
endmodule

module Adder1 (
  input  A0,
  input  A1,
  input  A2,
  output SUM,
  output CAL
);

  wire half_adder_1_cal, half_adder_1_sum, half_adder_2_cal;

  Half_Adder half_adder_1 (.A0(A0), .A1(A1), .SUM(half_adder_1_sum), .CAL(half_adder_1_cal));
  Half_Adder half_adder_2 (.A0(half_adder_1_sum), .A1(A2), .SUM(SUM), .CAL(half_adder_2_cal));
  or or_1 (CAL, half_adder_2_cal, half_adder_1_cal);
endmodule

module DEC_3To8 (
  input  A0,
  input  A1,
  input  A2,
  output Y0,
  output Y1,
  output Y2,
  output Y3,
  output Y4,
  output Y5,
  output Y6,
  output Y7
);

  wire A0_t, A1_t, B0, B1, C0, C1;

  DEC_1To2 dec_1to2_1 (.A0(A0), .Y0(A0_t), .Y1(A1_t));
  DEC_1To2 dec_1to2_2 (.A0(A1), .Y0(B0), .Y1(B1));
  DEC_1To2 dec_1to2_3 (.A0(A2), .Y0(C0), .Y1(C1));
  AND_with_3in and_with_3in_1 (.A0(A0_t), .A1(B0), .A2(C0), .Y0(Y0));
  AND_with_3in and_with_3in_2 (.A0(A1_t), .A1(B0), .A2(C0), .Y0(Y1));
  AND_with_3in and_with_3in_3 (.A0(A0_t), .A1(B1), .A2(C0), .Y0(Y2));
  AND_with_3in and_with_3in_4 (.A0(A1_t), .A1(B1), .A2(C0), .Y0(Y3));
  AND_with_3in and_with_3in_5 (.A0(A0_t), .A1(B0), .A2(C1), .Y0(Y4));
  AND_with_3in and_with_3in_6 (.A0(A1_t), .A1(B0), .A2(C1), .Y0(Y5));
  AND_with_3in and_with_3in_7 (.A0(A0_t), .A1(B1), .A2(C1), .Y0(Y6));
  AND_with_3in and_with_3in_8 (.A0(A1_t), .A1(B1), .A2(C1), .Y0(Y7));
endmodule

module DEC_1To2 (
  input  A0,
  output Y0,
  output Y1
);

  not not_1 (Y0, A0);

  assign Y1 = A0;
endmodule

module AND_with_3in (
  input  A0,
  input  A1,
  input  A2,
  output Y0
);

  wire and_1_out;

  and and_1 (and_1_out, A0, A1);
  and and_2 (Y0, and_1_out, A2);
endmodule

module DEC_4To16 (
  input  in_1,
  input  in_2,
  input  in_3,
  input  in_4
);

  wire A0, A1, A2, A3, A4, A5, A6, A7, B0, B1, B2, B3, B4, B5, B6, B7;

  DEC_3To8 DEC_A (
    .A0(in_1), .A1(in_2), .A2(in_3), .Y0(A0), .Y1(A1), .Y2(A2), .Y3(A3), .Y4(A4), .Y5(A5), .Y6(A6), .Y7(A7));
  DEC_3To8 DEC_B (
    .A0(in_2), .A1(in_3), .A2(in_4), .Y0(B0), .Y1(B1), .Y2(B2), .Y3(B3), .Y4(B4), .Y5(B5), .Y6(B6), .Y7(B7));
  // AND_Gate and_1 has open pins: in0=A0, in1=B0, out=open

  // Notes on the sheet:
  //   标签位置 →东
endmodule
