// Logisim project homework.circ as structural Verilog: 13 circuits, main circuit DEC_2To4
module main (
  input  in_1,
  input  in_2,
  input  in_3,
  input  in_4,
  input  in_5,
  input  in_6,
  input  in_7,
  input  in_8,
  input  in_9,
  input  in_10,
  input  in_11,
  input  in_12,
  input  in_13,
  input  in_14,
  input  in_15,
  input  in_16,
  input  in_17,
  input  in_18,
  input  in_19,
  input  in_20,
  input  in_21,
  input  in_22,
  input  in_23,
  input  in_24,
  input  in_25,
  input  in_26,
  input  in_27,
  input  in_28,
  input  in_29,
  input  in_30,
  input  in_31,
  input  in_32,
  input  in_33,
  input  in_34,
  input  in_35,
  input  in_36,
  input  in_37,
  input  in_38,
  input  in_39,
  input  in_40,
  input  in_41,
  input  in_42,
  input  in_43,
  input  in_44,
  input  in_45,
  input  in_46
);

  wire and_1_out, dec_2to4_1_y0, dec_2to4_1_y1, dec_2to4_1_y2, dec_2to4_1_y3, dec_3to8_1_y1, dec_3to8_1_y2,
       dec_3to8_1_y3, dec_3to8_1_y4, dec_3to8_1_y5, dec_3to8_1_y6, dec_3to8_1_y7, dec_3to8_1_y8,
       enc_4to2_1_y0, enc_4to2_1_y1, enc_16to4_1_y0, enc_16to4_1_y1, enc_16to4_1_y2, enc_16to4_1_y3,
       multiplexer_1_out, multiplexer_2_out, mux_2to1_1_y, mux_4to1_1_y, nand_1_out, nand_2_out, nand_3_out,
       nand_4_out, not_1_out, or_1_out, or_2_out, shumaguan_1_a, shumaguan_1_b, shumaguan_1_c, shumaguan_1_d,
       shumaguan_1_e, shumaguan_1_f, shumaguan_1_g;
  wire [1:0] priority_encoder_1_out;
  wire [3:0] enc_16to4_1_y_16;

  nand nand_1 (nand_1_out, in_1, in_2);
  or or_1 (or_1_out, in_1, in_2);
  nand nand_2 (nand_2_out, in_3, in_4);
  or or_2 (or_2_out, in_3, in_4);
  Hex_Digit_Display TEST (.value({in_16, in_15, in_14, in_13}));  // open: dp
  and and_1 (and_1_out, nand_1_out, or_1_out);
  LED XOR_OUT (.in(and_1_out));
  nand nand_3 (nand_3_out, nand_2_out, or_2_out);
  LED XNOR_OUT (.in(nand_3_out));
  not not_1 (not_1_out, in_17);
  LED led_1 (.in(priority_encoder_1_out[0]));
  LED led_2 (.in(priority_encoder_1_out[1]));
  Priority_Encoder #(.select(2)) priority_encoder_1 (
    .in0(in_34), .in1(in_35), .in2(in_36), .in3(in_37), .out(priority_encoder_1_out));  // open: gs, en_out, en_in
  Multiplexer multiplexer_1 (.in0(in_38), .in1(in_39), .out(multiplexer_1_out), .sel(in_40));
  Multiplexer #(.select(2)) multiplexer_2 (
    .in0(in_41), .in1(in_42), .in2(in_43), .in3(in_44), .out(multiplexer_2_out), .sel({in_46, in_45}));
  LED led_3 (.in(dec_2to4_1_y0));
  DEC_2To4 dec_2to4_1 (
    .A0(in_5), .A1(in_6), .EN(in_7), .Y0(dec_2to4_1_y0), .Y1(dec_2to4_1_y1), .Y2(dec_2to4_1_y2),
    .Y3(dec_2to4_1_y3));
  LED led_4 (.in(dec_2to4_1_y1));
  LED led_5 (.in(dec_2to4_1_y2));
  LED led_6 (.in(dec_2to4_1_y3));
  DEC_3To8 dec_3to8_1 (
    .A0(in_8), .A1(in_9), .A2(in_10), .EN(in_11), .Y1(dec_3to8_1_y1), .Y2(dec_3to8_1_y2), .Y3(dec_3to8_1_y3),
    .Y4(dec_3to8_1_y4), .Y5(dec_3to8_1_y5), .Y6(dec_3to8_1_y6), .Y7(dec_3to8_1_y7), .Y8(dec_3to8_1_y8));
  shumaguan shumaguan_1 (
    .A0(in_13), .A1(in_14), .A2(in_15), .A3(in_16), .EN(in_17), .A(shumaguan_1_a), .B(shumaguan_1_b),
    .C(shumaguan_1_c), .D(shumaguan_1_d), .E(shumaguan_1_e), .F(shumaguan_1_f), .G(shumaguan_1_g));
  ENC_16To4 enc_16to4_1 (
    .A0(in_18), .A1(in_19), .A2(in_20), .A3(in_21), .A4(in_22), .A5(in_23), .A6(in_24), .A7(in_25),
    .A8(in_26), .A9(in_27), .A10(in_28), .A11(in_29), .A12(in_30), .A13(in_31), .A14(in_32), .A15(in_33),
    .Y3(enc_16to4_1_y3), .Y2(enc_16to4_1_y2), .Y1(enc_16to4_1_y1), .Y0(enc_16to4_1_y0),
    .Y_16(enc_16to4_1_y_16));
  LedBar ledbar_1 (
    .led0(dec_3to8_1_y1), .led1(dec_3to8_1_y2), .led2(dec_3to8_1_y3), .led3(dec_3to8_1_y4),
    .led4(dec_3to8_1_y5), .led5(dec_3to8_1_y6), .led6(dec_3to8_1_y7), .led7(dec_3to8_1_y8));
  _7_Segment_Display u_7_segment_display_1 (
    .g(shumaguan_1_g), .f(shumaguan_1_f), .a(shumaguan_1_a), .b(shumaguan_1_b), .e(shumaguan_1_e),
    .d(shumaguan_1_d), .c(shumaguan_1_c), .dp(not_1_out));
  LedBar #(.matrixcols(4)) ledbar_2 (
    .led0(enc_16to4_1_y3), .led1(enc_16to4_1_y2), .led2(enc_16to4_1_y1), .led3(enc_16to4_1_y0));
  LED led_7 (.in(enc_4to2_1_y1));
  ENC_4To2 enc_4to2_1 (.A0(in_34), .A1(in_35), .A2(in_36), .A3(in_37), .Y1(enc_4to2_1_y1), .Y0(enc_4to2_1_y0));
  LED led_8 (.in(enc_4to2_1_y0));
  LED led_9 (.in(mux_2to1_1_y));
  MUX_2To1 mux_2to1_1 (.D0(in_38), .D1(in_39), .S(in_40), .Y(mux_2to1_1_y));
  LED led_10 (.in(multiplexer_1_out));
  LED led_11 (.in(mux_4to1_1_y));
  MUX_4To1 mux_4to1_1 (.D0(in_41), .D1(in_42), .D2(in_43), .D3(in_44), .S0(in_45), .S1(in_46), .Y(mux_4to1_1_y));
  LED led_12 (.in(multiplexer_2_out));
  Decoder #(.select(2)) decoder_1 ();  // open: out0, out1, out2, out3, sel, en
  Hex_Digit_Display hex_digit_display_1 (.value(enc_16to4_1_y_16));  // open: dp
  nand nand_4 (nand_4_out, enc_16to4_1_y_16[0], enc_16to4_1_y_16[1], enc_16to4_1_y_16[2], enc_16to4_1_y_16[3]);
  Decoder #(.select(3)) decoder_2 ();  // open: out0, out1, out2, out3, out4, out5, out6, out7, sel, en
  Priority_Encoder #(.select(4)) priority_encoder_2 ();  // open: in0, in1, in2, in3, in4, in5, in6, in7, in8, in9, in10, in11, in12, in13, in14, in15, out, gs, en_out, en_in

  // Notes on the sheet:
  //   异或门
  //   同或门
  //   2-4译码器
  //   16-4编码器
  //   4-2优先编码器
  //   2-1选择器
  //   4-1选择器
  //   7段数码管译码器
  //   3-8译码器
endmodule

module DEC_1To2 (
  input  A0,
  output Y0,
  output Y1
);

  not not_1 (Y0, A0);

  assign Y1 = A0;
endmodule

module DEC_2To4 (
  input  A0,
  input  A1,
  input  EN,
  output Y0,
  output Y1,
  output Y2,
  output Y3
);

  wire not_1_out, not_2_out;

  not not_1 (not_1_out, A0);
  not not_2 (not_2_out, A1);
  and and_1 (Y0, not_1_out, EN, not_2_out);
  and and_2 (Y1, not_1_out, EN, A1);
  and and_3 (Y2, A0, EN, not_2_out);
  and and_4 (Y3, A0, EN, A1);
endmodule

module DEC_3To8 (
  input  A0,
  input  A1,
  input  A2,
  input  EN,
  output Y1,
  output Y2,
  output Y3,
  output Y4,
  output Y5,
  output Y6,
  output Y7,
  output Y8
);

  wire and_1_out, and_2_out, not_1_out;

  not not_1 (not_1_out, A2);
  and and_1 (and_1_out, not_1_out, EN);
  and and_2 (and_2_out, A2, EN);
  DEC_2To4 dec_2to4_1 (.A0(A1), .A1(A0), .EN(and_1_out), .Y0(Y1), .Y1(Y2), .Y2(Y3), .Y3(Y4));
  DEC_2To4 dec_2to4_2 (.A0(A1), .A1(A0), .EN(and_2_out), .Y0(Y5), .Y1(Y6), .Y2(Y7), .Y3(Y8));
endmodule

module DEC_4To16 (
  input  A0,
  input  A1,
  input  A2,
  input  A3,
  input  EN,
  output Y0,
  output Y1,
  output Y2,
  output Y3,
  output Y4,
  output Y5,
  output Y6,
  output Y7,
  output Y8,
  output Y9,
  output Y10,
  output Y11,
  output Y12,
  output Y13,
  output Y14,
  output Y15
);

  wire and_1_out, and_2_out, not_1_out;

  not not_1 (not_1_out, A3);
  and and_1 (and_1_out, EN, A3);
  and and_2 (and_2_out, not_1_out, EN);
  DEC_3To8 dec_3to8_1 (
    .A0(A0), .A1(A1), .A2(A2), .EN(and_2_out), .Y1(Y0), .Y2(Y1), .Y3(Y2), .Y4(Y3), .Y5(Y4), .Y6(Y5), .Y7(Y6),
    .Y8(Y7));
  DEC_3To8 dec_3to8_2 (
    .A0(A0), .A1(A1), .A2(A2), .EN(and_1_out), .Y1(Y8), .Y2(Y9), .Y3(Y10), .Y4(Y11), .Y5(Y12), .Y6(Y13),
    .Y7(Y14), .Y8(Y15));
endmodule

module shumaguan (
  input  A0,
  input  A1,
  input  A2,
  input  A3,
  input  EN,
  output A,
  output B,
  output C,
  output D,
  output E,
  output F,
  output G
);

  wire dec_4to16_1_y0, dec_4to16_1_y1, dec_4to16_1_y2, dec_4to16_1_y3, dec_4to16_1_y4, dec_4to16_1_y5,
       dec_4to16_1_y6, dec_4to16_1_y7, dec_4to16_1_y8, dec_4to16_1_y9, dec_4to16_1_y10, dec_4to16_1_y11,
       dec_4to16_1_y12, dec_4to16_1_y13, dec_4to16_1_y14, dec_4to16_1_y15;

  DEC_4To16 dec_4to16_1 (
    .A0(A0), .A1(A1), .A2(A2), .A3(A3), .EN(EN), .Y0(dec_4to16_1_y0), .Y1(dec_4to16_1_y1),
    .Y2(dec_4to16_1_y2), .Y3(dec_4to16_1_y3), .Y4(dec_4to16_1_y4), .Y5(dec_4to16_1_y5), .Y6(dec_4to16_1_y6),
    .Y7(dec_4to16_1_y7), .Y8(dec_4to16_1_y8), .Y9(dec_4to16_1_y9), .Y10(dec_4to16_1_y10),
    .Y11(dec_4to16_1_y11), .Y12(dec_4to16_1_y12), .Y13(dec_4to16_1_y13), .Y14(dec_4to16_1_y14),
    .Y15(dec_4to16_1_y15));
  or or_1 (A, dec_4to16_1_y0, dec_4to16_1_y2, dec_4to16_1_y3, dec_4to16_1_y5, dec_4to16_1_y6, dec_4to16_1_y7, dec_4to16_1_y8, dec_4to16_1_y9, dec_4to16_1_y10, dec_4to16_1_y12, dec_4to16_1_y14, dec_4to16_1_y15);
  or or_2 (B, dec_4to16_1_y0, dec_4to16_1_y1, dec_4to16_1_y2, dec_4to16_1_y3, dec_4to16_1_y4, dec_4to16_1_y7, dec_4to16_1_y8, dec_4to16_1_y9, dec_4to16_1_y10, dec_4to16_1_y13);
  or or_3 (C, dec_4to16_1_y0, dec_4to16_1_y1, dec_4to16_1_y3, dec_4to16_1_y4, dec_4to16_1_y5, dec_4to16_1_y6, dec_4to16_1_y7, dec_4to16_1_y8, dec_4to16_1_y9, dec_4to16_1_y10, dec_4to16_1_y11, dec_4to16_1_y13);
  or or_4 (D, dec_4to16_1_y0, dec_4to16_1_y2, dec_4to16_1_y3, dec_4to16_1_y5, dec_4to16_1_y6, dec_4to16_1_y8, dec_4to16_1_y9, dec_4to16_1_y11, dec_4to16_1_y12, dec_4to16_1_y13, dec_4to16_1_y14);
  or or_5 (E, dec_4to16_1_y0, dec_4to16_1_y2, dec_4to16_1_y6, dec_4to16_1_y8, dec_4to16_1_y10, dec_4to16_1_y11, dec_4to16_1_y12, dec_4to16_1_y13, dec_4to16_1_y14, dec_4to16_1_y15);
  or or_6 (F, dec_4to16_1_y0, dec_4to16_1_y4, dec_4to16_1_y5, dec_4to16_1_y6, dec_4to16_1_y8, dec_4to16_1_y9, dec_4to16_1_y10, dec_4to16_1_y11, dec_4to16_1_y12, dec_4to16_1_y14, dec_4to16_1_y15);
  or or_7 (G, dec_4to16_1_y2, dec_4to16_1_y3, dec_4to16_1_y4, dec_4to16_1_y5, dec_4to16_1_y6, dec_4to16_1_y8, dec_4to16_1_y9, dec_4to16_1_y10, dec_4to16_1_y11, dec_4to16_1_y13, dec_4to16_1_y14, dec_4to16_1_y15);
endmodule

module ENC_16To4 (
  input  A0,
  input  A1,
  input  A2,
  input  A3,
  input  A4,
  input  A5,
  input  A6,
  input  A7,
  input  A8,
  input  A9,
  input  A10,
  input  A11,
  input  A12,
  input  A13,
  input  A14,
  input  A15,
  output Y3,
  output Y2,
  output Y1,
  output Y0,
  output [3:0] Y_16
);

  or or_1 (Y3, A15, A14, A13, A12, A11, A10, A9, A8);
  or or_2 (Y2, A4, A5, A6, A7, A12, A13, A14, A15);
  or or_3 (Y1, A2, A3, A6, A7, A10, A11, A14, A15);
  or or_4 (Y0, A1, A3, A5, A7, A9, A11, A13, A15);

  assign Y_16 = {Y3, Y2, Y1, Y0};
endmodule

module ENC_4To2 (
  input  A0,
  input  A1,
  input  A2,
  input  A3,
  output Y1,
  output Y0
);

  wire and_1_out, not_1_out;

  // NoConnect on A0
  or or_1 (Y1, A2, A3);
  not not_1 (not_1_out, Y1);
  and and_1 (and_1_out, not_1_out, A1);
  or or_2 (Y0, and_1_out, A3);
endmodule

module MUX_2To1 (
  input  D0,
  input  D1,
  input  S,
  output Y
);

  wire and_1_out, and_2_out, dec_1to2_1_y0, dec_1to2_1_y1;

  DEC_1To2 dec_1to2_1 (.A0(S), .Y0(dec_1to2_1_y0), .Y1(dec_1to2_1_y1));
  and and_1 (and_1_out, D0, dec_1to2_1_y0);
  and and_2 (and_2_out, dec_1to2_1_y1, D1);
  or or_1 (Y, and_1_out, and_2_out);
endmodule

module MUX_4To1 (
  input  D0,
  input  D1,
  input  D2,
  input  D3,
  input  S0,
  input  S1,
  output Y
);

  wire A0, A1, A2, A3, and_1_out, and_2_out, and_3_out, and_4_out;

  and and_1 (and_1_out, D0, A0);
  and and_2 (and_2_out, D1, A1);
  and and_3 (and_3_out, D2, A2);
  and and_4 (and_4_out, D3, A3);
  or or_1 (Y, and_1_out, and_2_out, and_3_out, and_4_out);
  DEC_2To4 dec_2to4_1 (.A0(S1), .A1(S0), .EN(1'b1), .Y0(A0), .Y1(A1), .Y2(A2), .Y3(A3));
endmodule

module keqiehuanjinwei (
  input  in_1,
  input  in_2,
  input  in_3,
  input  in_4,
  input  in_5
);

  DEC_4To16 dec_4to16_1 (
    .A0(in_1), .A1(in_2), .A2(in_3), .A3(in_4));  // open: EN, Y0, Y1, Y2, Y3, Y4, Y5, Y6, Y7, Y8, Y9, Y10, Y11, Y12, Y13, Y14, Y15
endmodule

module Half_Adder (
  input  A0,
  input  A1,
  output SUM,
  output CAL
);

  xor xor_1 (SUM, A0, A1);
  and and_1 (CAL, A0, A1);
endmodule

module Full_Adder (
  input  in_1,
  input  in_2,
  input  in_3,
  output SUM,
  output CAL
);

  wire half_adder_1_cal, half_adder_1_sum, half_adder_2_cal;

  Half_Adder half_adder_1 (.A0(in_1), .A1(in_2), .SUM(half_adder_1_sum), .CAL(half_adder_1_cal));
  Half_Adder half_adder_2 (.A0(half_adder_1_sum), .A1(in_3), .SUM(SUM), .CAL(half_adder_2_cal));
  or or_1 (CAL, half_adder_2_cal, half_adder_1_cal);
endmodule
